// Logisim project datapath.circ as structural Verilog: 3 circuits, main circuit datapath
module datapath (
  input  in_1,
  input  in_2,
  input  in_3,
  input  in_4,
  input  in_5,
  input  [1:0] in_6,
  input  [3:0] in_7,
  input  in_8,
  input  in_9,
  input  in_10,
  input  in_11,
  input  in_12,
  input  in_13,
  input  in_14,
  input  in_15,
  input  in_16,
  output out_17,
  output [3:0] out_18,
  output [3:0] out_19,
  output [3:0] out_20,
  output [2:0] out_21
);

  wire comparator_1_eq, comparator_2_eq, not_1_out;
  wire [4:4] IR_q;
  wire [15:0] A_q, alu_1_out, B_q, bit_extender_1_out, controlled_buffer_1_out, MAR_q, multiplexer_1_out,
       PC_q, ram_1_data, ram_2_data;

  Register #(.width(16)) PC (.D(controlled_buffer_1_out), .en(in_5), .Q(PC_q), .clk(in_15));  // open: clr
  assign controlled_buffer_1_out = in_10 ? PC_q : 16'bz;  // Controlled_Buffer controlled_buffer_1
  Register #(.width(16)) A (.D(controlled_buffer_1_out), .en(in_1), .Q(A_q), .clk(in_15));  // open: clr
  ALU alu_1 (.A(A_q), .B(B_q), .func(in_6), .out(alu_1_out));
  Register #(.width(1)) Z (.D(comparator_1_eq), .en(in_16), .Q(out_17), .clk(in_15));  // open: clr
  assign controlled_buffer_1_out = in_11 ? alu_1_out : 16'bz;  // Controlled_Buffer controlled_buffer_2
  Comparator #(.width(16)) comparator_1 (
    .a(controlled_buffer_1_out), .b({16{1'b0}}), .eq(comparator_1_eq));  // open: gt, lt
  Register #(.width(16)) B (.D(controlled_buffer_1_out), .en(in_2), .Q(B_q), .clk(in_15));  // open: clr
  Comparator #(.width(4)) comparator_2 (.a(in_7), .b(4'b0000), .eq(comparator_2_eq));  // open: gt, lt
  RAM #(.addrWidth(4), .dataWidth(16), .bus("separate")) ram_1 (
    .addr(in_7), .din(controlled_buffer_1_out), .data(ram_1_data), .str(in_3), .clk(in_15));  // open: sel, ld, clr
  not not_1 (not_1_out, comparator_2_eq);
  Multiplexer #(.width(16), .enable("false")) multiplexer_1 (
    .in0({16{1'b0}}), .in1(ram_1_data), .out(multiplexer_1_out), .sel(not_1_out));
  assign controlled_buffer_1_out = in_12 ? multiplexer_1_out : 16'bz;  // Controlled_Buffer controlled_buffer_3
  Register #(.width(16)) MAR (.D(controlled_buffer_1_out), .en(in_4), .Q(MAR_q), .clk(in_15));  // open: clr
  RAM #(.addrWidth(16), .dataWidth(16), .bus("separate")) ram_2 (
    .addr(MAR_q), .din(controlled_buffer_1_out), .data(ram_2_data), .str(in_8), .clk(in_15));  // open: sel, ld, clr
  assign controlled_buffer_1_out = in_13 ? ram_2_data : 16'bz;  // Controlled_Buffer controlled_buffer_4
  Register #(.width(16)) IR (
    .D(controlled_buffer_1_out), .en(in_9), .Q({out_21, out_18, out_19, IR_q[4], out_20}), .clk(in_15));  // open: clr
  assign bit_extender_1_out = {{11{IR_q[4]}}, {IR_q[4], out_20}};  // Bit_Extender bit_extender_1
  assign controlled_buffer_1_out = in_14 ? bit_extender_1_out : 16'bz;  // Controlled_Buffer controlled_buffer_5

  // Other names for the same wires on the sheet: RZ[3:0] = out_20; RY[3:0] = out_19; RX[3:0] = out_18;
  //   OP[2:0] = out_21; CLK = in_15; DrALU = in_11; DrMEM = in_13; DrOFF = in_14; DrPC = in_10; DrREG = in_12;
  //   func[1:0] = in_6; LdA = in_1; LdB = in_2; LdIR = in_9; LdMAR = in_4; LdPC = in_5; LdZ = in_16;
  //   regno[3:0] = in_7; WrMEM = in_8; WrREG = in_3; Z = out_17

  // Notes on the sheet:
  //   LC2200 Datapath, by Tim Martin
  //   Register File
  //   Memory
endmodule

module ALU (
  input  [15:0] A,
  input  [15:0] B,
  input  [1:0] func,
  output [15:0] out
);

  wire [15:0] adder_1_out, adder_2_out, nand_1_out, subtractor_1_out;

  Adder #(.width(16)) adder_1 (.a(A), .b(B), .out(adder_1_out));  // open: cin, cout
  assign nand_1_out = ~(A & B);  // NAND_Gate nand_1, 16 bits wide
  Subtractor #(.width(16)) subtractor_1 (.a(A), .b(B), .out(subtractor_1_out));  // open: bin, bout
  Adder #(.width(16)) adder_2 (.a(A), .b(16'h1), .out(adder_2_out));  // open: cin, cout
  Multiplexer #(.select(2), .width(16), .enable("false")) multiplexer_1 (
    .in0(adder_1_out), .in1(nand_1_out), .in2(subtractor_1_out), .in3(adder_2_out), .out(out), .sel(func));

  // Notes on the sheet:
  //   ALU, by Tim Martin
endmodule

module microcontrol_unit (
  input  [2:0] OP,
  input  Z,
  input  in_3
);

  wire ALUHi, ALULo, chkZ, DrALU, DrMEM, DrOFF, DrPC, DrReg, LdA, LdB, LdIR, LdMAR, LdPC, LdZ, OPTest,
       RegSelHi, RegSelLo, WrMEM, WrREG;
  wire [5:0] multiplexer_1_out, nState, OPdata, State, Zdata;

  ROM #(.addrWidth(6), .dataWidth(25)) rom_1 (
    .addr(State),
    .data({chkZ, OPTest, ALUHi, ALULo, RegSelHi, RegSelLo, WrMEM, WrREG, LdZ, LdB, LdA, LdMAR, LdIR, LdPC, DrOFF, DrPC, DrALU, DrMEM, DrReg, nState}));  // open: sel
  ROM #(.addrWidth(3), .dataWidth(6)) rom_2 (.addr(OP), .data(OPdata));  // open: sel
  ROM #(.addrWidth(2), .dataWidth(6)) rom_3 (.addr({1'b0, Z}), .data(Zdata));  // open: sel
  Multiplexer #(.select(2), .width(6), .enable("false")) multiplexer_1 (
    .in0(nState), .in1(OPdata), .in2(Zdata), .out(multiplexer_1_out), .sel({chkZ, OPTest}));  // open: in3
  Register #(.width(6)) State_Register (.D(multiplexer_1_out), .Q(State), .clk(in_3));  // open: en, clr

  // Other names for the same wires on the sheet: CLK = in_3

  // Notes on the sheet:
  //   Main ROM
  //   OpCheck ROM
  //   OnZ ROM
endmodule
